# Fritzing sketch nyomógomb_fényerő (3) (saved by Fritzing 0.9.9b)
breadboards: 1

parts:
  Mod1 = Raspberry Pi 4B
  R5 = Resistor [tolerance=±5% power=0pW resistance=3.3k package=THT]
  R6 = Resistor [tolerance=±5% power=0pW resistance=10 package=THT]
  S1 = Pushbutton [package="[THT]"]
  S2 = Pushbutton [package="[THT]"]
  R1 = Resistor [tolerance=±5% power=0.25 resistance=3.3k package=THT]
  R7 = Resistor [tolerance=±5% power=0.25 resistance=10 package=THT]
  R3 = Resistor [tolerance=±5% power=0.25 resistance=220 package=THT]
  W = LED - 5mm [color="Green (570nm)" current=0.030 package="5 mm [THT]"]

nets:
  N1: Mod1.3V3, W.anode
  N2: Mod1.GPIO27, R3.Pin_1
  N3: Mod1.GPIO13, R1.Pin_1
  N4: Mod1.GPIO16, R5.Pin_0
  N5: Mod1.GND, S1.Pin_1, S1.Pin_2, S2.Pin_3, S2.Pin_4
  N6: R5.Pin_1, R6.Pin_0, S1.Pin_3, S1.Pin_4
  N7: R6.Pin_1, R7.Pin_1
  N8: S2.Pin_2, R1.Pin_0, R7.Pin_0
  N9: R3.Pin_0, W.cathode
