# Fritzing sketch nyomógomb_fényerő másolata (saved by Fritzing 0.9.9b)
breadboards: 1

parts:
  Mod1 = Raspberry Pi 4B
  R5 = Resistor [tolerance=±5% power=0pW resistance=3.3k package=THT]
  R6 = Resistor [tolerance=±5% power=0pW resistance=10k package=THT]
  S1 = Pushbutton [package="[THT]"]
  S2 = Pushbutton [package="[THT]"]
  R1 = Resistor [tolerance=±5% power=0.25 resistance=3.3k package=THT]
  R7 = Resistor [tolerance=±5% power=0.25 resistance=10k package=THT]
  R8 = Resistor [tolerance=±5% power=0.25 resistance=0 package=THT]
  R3 = Resistor [tolerance=±5% power=0.25 resistance=220 package=THT]
  R4 = Resistor [tolerance=±5% power=0.25 resistance=3.3k package=THT]
  B = LED - 5mm [color="Blue (505nm)" current=0.030 package="5 mm [THT]"]
  G = LED - 5mm [color="Green (570nm)" current=0.030 package="5 mm [THT]"]
  R = LED - 5mm [color="Red (635nm)" current=0.030 package="5 mm [THT]"]

nets:
  N1: Mod1.3V3, B.anode, G.anode, R.anode
  N2: Mod1.GPIO17, R4.Pin_1
  N3: Mod1.GPIO22, R3.Pin_1
  N4: Mod1.GPIO9, R8.Pin_1
  N5: Mod1.GPIO13, R1.Pin_1
  N6: Mod1.GPIO16, R5.Pin_0
  N7: Mod1.GND, S1.Pin_1, S1.Pin_2, S2.Pin_3, S2.Pin_4
  N8: R5.Pin_1, R6.Pin_0, S1.Pin_3, S1.Pin_4
  N9: R6.Pin_1, R7.Pin_1
  N10: S2.Pin_2, R1.Pin_0, R7.Pin_0
  N11: R8.Pin_0, R.cathode
  N12: R3.Pin_0, G.cathode
  N13: R4.Pin_0, B.cathode
